// Digital circuit SOMA.dig as structural Verilog
module SOMA (
  input  [4:0] A,
  input  [4:0] B,
  output [4:0] SOMA,
  output [4:0] carri
);

  Add #(.Bits(5)) add_1 (.a(A), .b(B), .c_i(1'b0), .s(SOMA), .c_o(carri[0]));
  // Pins of 1 and 5 bits meet at carri
endmodule
