// Digital circuit Seletor.dig as structural Verilog
module Seletor (
  input  [2:0] in_1
);

  wire undriven, undriven_2;

  Demultiplexer #(.Selector_Bits(3)) demultiplexer_1 (
    .sel(in_1), .in(undriven));  // open: out_0, out_1, out_2, out_3, out_4, out_5, out_6, out_7
  Demultiplexer #(.Selector_Bits(3)) demultiplexer_2 (
    .sel(in_1), .in(undriven_2));  // open: out_0, out_1, out_2, out_3, out_4, out_5, out_6, out_7
  // Pins of 1 and 3 bits meet at in_1
endmodule
