// Digital circuit divisorDeBits.dig as structural Verilog
module divisorDeBits (
  input  [4:0] A,
  output S0,
  output S1,
  output S2,
  output S3
);

  wire [7:0] bitextender_1_out;

  BitSelector #(.Selector_Bits(3)) bitselector_1 (.in(bitextender_1_out), .sel(3'b000), .out(S0));
  BitSelector #(.Selector_Bits(3)) bitselector_2 (.in(bitextender_1_out), .sel(3'b001), .out(S1));
  BitSelector #(.Selector_Bits(3)) bitselector_3 (.in(bitextender_1_out), .sel(3'b010), .out(S2));
  BitSelector #(.Selector_Bits(3)) bitselector_4 (.in(bitextender_1_out), .sel(3'b011), .out(S3));
  BitExtender #(.inputBits(5), .outputBits(8)) bitextender_1 (.in(A), .out(bitextender_1_out));
endmodule
