// Digital circuit funcoesBooleanas.dig as structural Verilog
module funcoesBooleanas (
  input  in_1,
  input  in_2,
  input  in_4,
  input  in_5,
  input  in_6,
  output out_3
);

  wire and_1_out, and_2_out, and_3_out, and_4_out, and_5_out, and_6_out, and_7_out, and_8_out, and_9_out,
       comparator_1_gt, comparator_2_eq, comparator_3_lt, not_1_out, or_1_out, or_2_out, or_3_out, or_4_out,
       or_5_out, or_6_out, or_7_out, or_8_out, or_9_out;

  and and_1 (and_1_out, in_4, in_6);
  and and_2 (and_2_out, in_4, in_5);
  and and_3 (and_3_out, in_6, in_5);
  and and_4 (and_4_out, not_1_out, and_1_out);
  and and_5 (and_5_out, and_3_out, in_4);
  and and_6 (and_6_out, and_2_out, not_1_out);
  not not_1 (not_1_out, and_5_out);
  Comparator comparator_1 (.a(in_1), .b(in_2), .gt(comparator_1_gt));  // open: eq, lt
  Comparator comparator_2 (.a(in_1), .b(in_2), .eq(comparator_2_eq));  // open: gt, lt
  Comparator comparator_3 (.a(in_1), .b(in_2), .lt(comparator_3_lt));  // open: gt, eq
  or or_1 (or_1_out, and_4_out, 1'b0);
  Seven_Seg seven_seg_1 (.a(1'b0), .b(1'b0), .c(1'b0), .d(1'b0), .e(1'b0), .f(1'b0), .g(1'b0), .dp(1'b0));
  or or_2 (or_2_out, and_6_out, 1'b0);
  Seven_Seg seven_seg_2 (
    .a(1'b0), .b(1'b0), .c(or_1_out), .d(or_8_out), .e(or_2_out), .f(1'b0), .g(or_9_out), .dp(1'b0));
  and and_7 (and_7_out, and_4_out, comparator_1_gt);
  and and_8 (and_8_out, and_5_out, comparator_2_eq);
  and and_9 (and_9_out, comparator_3_lt, and_6_out);
  or or_3 (or_3_out, and_4_out, and_6_out);
  or or_4 (or_4_out, and_4_out, and_6_out);
  or or_5 (or_5_out, or_3_out, and_5_out);
  or or_6 (or_6_out, or_4_out, and_5_out);
  or or_7 (or_7_out, and_7_out, and_8_out);
  or or_8 (or_8_out, or_6_out, 1'b0);
  or or_9 (or_9_out, or_5_out, 1'b0);
  or or_10 (out_3, or_7_out, and_9_out);
endmodule
