// Digital circuit modulo.dig as structural Verilog
module modulo (
  input  [4:0] S2,
  output [4:0] modulo,
  output [4:0] sinal
);

  wire relaydt_1_p3;
  wire [4:0] neg_1_out, relaydt_1_p2;

  // sinal sinal_1: pin names not known; wires that end beside it: S2, sinal, sinal, 1'b0
  // RelayDT #(.Bits(5)) relaydt_1: pin names not known; wires that end beside it: S2, relaydt_1_p2, relaydt_1_p3
  Neg #(.Bits(5)) neg_1 (.in(relaydt_1_p2), .out(neg_1_out));
  // RelayDT #(.Bits(5)) relaydt_2: pin names not known; wires that end beside it: relaydt_1_p3, neg_1_out, 1'b0, modulo, sinal
endmodule
