// Digital circuit sinal.dig as structural Verilog
module sinal (
  input  [4:0] S0,
  output Sinal
);

  wire comparator_1_eq, comparator_1_gt, comparator_1_lt, nor_1_out;

  Comparator #(.Bits(5)) comparator_1 (
    .a(S0), .b(5'b01111), .gt(comparator_1_gt), .eq(comparator_1_eq), .lt(comparator_1_lt));
  nor nor_1 (nor_1_out, comparator_1_eq, comparator_1_lt);
  or or_1 (Sinal, comparator_1_gt, nor_1_out);
endmodule
