// Digital circuit soma.dig as structural Verilog
module soma (
  input  [4:0] A,
  input  [4:0] B,
  output [4:0] SOMA,
  output carri
);

  Add #(.Bits(5)) add_1 (.a(A), .b(B), .c_i(1'b0), .s(SOMA), .c_o(carri));
endmodule
