// Digital circuit somaDisplay.dig as structural Verilog
module somaDisplay (
  input  [4:0] A,
  input  [4:0] B,
  input  enable
);

  wire _7448_1_p10, _7448_1_p11, _7448_1_p12, _7448_1_p13, _7448_1_p14, _7448_1_p15, _7448_1_p16,
       divisordebits_1_s0, divisordebits_1_s1, divisordebits_1_s2, divisordebits_1_s3, somafinal_1_sinal;
  wire [4:0] somafinal_1_somafinalemmodulo;

  somaFinal somafinal_1 (
    .A(A), .B(B), .enable(enable), .somaFinalEmModulo(somafinal_1_somafinalemmodulo),
    .sinal(somafinal_1_sinal));
  divisorDeBits divisordebits_1 (
    .A(somafinal_1_somafinalemmodulo), .S0(divisordebits_1_s0), .S1(divisordebits_1_s1),
    .S2(divisordebits_1_s2), .S3(divisordebits_1_s3));
  // _7448 _7448_1: pin names not known; wires that end beside it: divisordebits_1_s0, divisordebits_1_s1, divisordebits_1_s2, divisordebits_1_s3, 1'b1, 1'b1, 1'b1, 1'b0, 1'b1, _7448_1_p10, _7448_1_p11, _7448_1_p12, _7448_1_p13, _7448_1_p14, _7448_1_p15, _7448_1_p16
  LED led_1 (.in(somafinal_1_sinal));
  Seven_Seg #(.commonCathode("true")) seven_seg_1 (
    .a(_7448_1_p10), .b(_7448_1_p11), .c(_7448_1_p12), .d(_7448_1_p13), .e(_7448_1_p14), .f(_7448_1_p15),
    .g(_7448_1_p16), .dp(1'b0), .common(1'b0));
endmodule
