// Digital circuit somaFinal.dig as structural Verilog
module somaFinal (
  input  [4:0] A,
  input  [4:0] B,
  input  enable,
  output [4:0] somaFinalEmModulo,
  output [4:0] sinal
);

  wire [4:0] relay_1_p5, relay_2_p2, soma_1_soma;

  // Relay #(.Bits(5)) relay_1: pin names not known; wires that end beside it: enable, A, enable, 1'b0, relay_1_p5, 1'b0
  // Relay #(.Bits(5)) relay_2: pin names not known; wires that end beside it: B, relay_2_p2
  soma soma_1 (.A(relay_1_p5), .B(relay_2_p2), .SOMA(soma_1_soma));  // open: carri
  modulo modulo_1 (.S2(soma_1_soma), .modulo(somaFinalEmModulo), .sinal(sinal));
  // Pins of 1 and 5 bits meet at sinal

  // Other names for the same wires on the sheet: e1 = enable
endmodule
