// Digital circuit subtração.dig as structural Verilog
module \subtração  (
  input  [4:0] A,
  input  [4:0] B,
  output [4:0] SOMA,
  output [4:0] carri
);

  Sub #(.Bits(5)) sub_1 (.a(A), .b(B), .c_i(1'b0), .s(SOMA), .c_o(carri[0]));
  // Pins of 1 and 5 bits meet at carri
endmodule
