// Digital circuit xnor.dig as structural Verilog
module \xnor  (
  input  [4:0] A,
  input  [4:0] B,
  output [4:0] AND
);

  // XNOr xnor_1 has open pins: In_1=A[0], In_2=B[0], out=open
  // Pins of 1 and 5 bits meet at A
  // Pins of 1 and 5 bits meet at B
endmodule
